# Fritzing sketch schematic (saved by Fritzing 0.7.10b)
breadboards: 1

parts:
  Arduino1 = Arduino
  K1 = Relay [part_number=FRS1B-S package=THT]
  Fuse1 = Fuse with Handler [part_number=Htc-15m]
  R1 = Photocell (LDR) [package=THT]  # not connected
  R2 = Photocell (LDR) [package=THT]  # not connected
  RHT1 = Humidity and Temperature Sensor RHT03  # not connected
  Part1 = Bluetooth Mate Silver
  L1 = Solenoid
  R3 = Resistor [tolerance=±5% resistance=1k package=THT]
  Q1 = NPN-Transistor [package="TO92 [THT]"]
  D1 = Rectifier Diode [part_number=1N4001 package="300 mil [THT]"]
  Power_plug1 = Power plug

nets:
  N1: Arduino1.D2, R3.Pin_0
  N2: Arduino1.D1TX, Part1.RX_5V
  N3: Arduino1.D0RX, Part1.TX_5V
  N4: K1.A, Power_plug1.VCC
  N5: K1.COIL1, Part1.VCC
  N6: K1.COIL2, D1.anode
  N7: K1.B, Fuse1.Connector1
  N8: Fuse1.Connector2, L1.pin2
  N9: Part1.GND, Q1.E
  N10: L1.pin1, Power_plug1.GND
  N11: R3.Pin_1, Q1.B
  N12: Q1.C, D1.cathode
